// Logisim project control-logic.circ as structural Verilog: 1 circuit, main circuit control_logic
module control_logic (
  input  [31:0] inst,
  input  BrEq,
  input  BrLt,
  output PCSel,
  output RegWEn,
  output [2:0] ImmSel,
  output BrUn,
  output ASel,
  output BSel,
  output [3:0] ALUSel,
  output MemRW,
  output [1:0] WBSel,
  output CSRSel,
  output CSRWen
);

  wire and_8_out, and_9_out, and_10_out, and_11_out, and_12_out, b_instr, beq, bge, bgeu, big, blt, bltu,
       bne, br_pc, br_uns, not_1_out, not_2_out, not_3_out, not_4_out, not_5_out, not_6_out, not_7_out,
       not_8_out, not_9_out, not_10_out, not_11_out, not_12_out, not_13_out, not_14_out, or_2_out, or_4_out,
       smol;
  wire [2:0] csr_imm;
  wire [3:0] ams, csr_op, i_op, r_op, sllmulh, sr;

  Multiplexer #(.enable("false"), .select(3), .width(3)) multiplexer_1 (
    .in1(3'b000), .in5(3'b101), .out(csr_imm), .sel(inst[14:12]));  // open: in0, in2, in3, in4, in6, in7
  Multiplexer #(.enable("false"), .select(5)) multiplexer_2 (
    .in0(1'b0), .in4(1'b0), .in5(1'b0), .in8(1'b0), .in12(1'b0), .in13(1'b0), .in24(br_pc), .in25(1'b1),
    .in27(1'b1), .in28(1'b0), .out(PCSel), .sel(inst[6:2]));  // open: in1, in2, in3, in6, in7, in9, in10, in11, in14, in15, in16, in17, in18, in19, in20, in21, in22, in23, in26, in29, in30, in31
  Multiplexer #(.enable("false"), .select(5), .width(3)) multiplexer_3 (
    .in0(3'b000), .in4(3'b000), .in5(3'b011), .in8(3'b001), .in12(3'b000), .in13(3'b011), .in24(3'b010),
    .in25(3'b000), .in27(3'b100), .in28(csr_imm), .out(ImmSel), .sel(inst[6:2]));  // open: in1, in2, in3, in6, in7, in9, in10, in11, in14, in15, in16, in17, in18, in19, in20, in21, in22, in23, in26, in29, in30, in31
  Multiplexer #(.enable("false"), .select(5), .width(4)) multiplexer_4 (
    .in0(4'b0000), .in4(i_op), .in5(4'b0000), .in8(4'b0000), .in12(r_op), .in13(4'b1111), .in24(4'b0000),
    .in25(4'b0000), .in27(4'b0000), .in28(csr_op), .out(ALUSel), .sel(inst[6:2]));  // open: in1, in2, in3, in6, in7, in9, in10, in11, in14, in15, in16, in17, in18, in19, in20, in21, in22, in23, in26, in29, in30, in31
  Multiplexer #(.enable("false"), .select(5)) multiplexer_5 (
    .in0(1'b0), .in4(1'b0), .in5(1'b0), .in8(1'b1), .in12(1'b0), .in13(1'b0), .in24(1'b0), .in25(1'b0),
    .in27(1'b0), .in28(1'b0), .out(MemRW), .sel(inst[6:2]));  // open: in1, in2, in3, in6, in7, in9, in10, in11, in14, in15, in16, in17, in18, in19, in20, in21, in22, in23, in26, in29, in30, in31
  not not_1 (not_1_out, inst[12]);
  not not_2 (not_2_out, inst[13]);
  not not_3 (not_3_out, inst[14]);
  not not_4 (not_4_out, inst[13]);
  not not_5 (not_5_out, inst[14]);
  not not_6 (not_6_out, inst[12]);
  not not_7 (not_7_out, inst[13]);
  Multiplexer #(.enable("false"), .select(2), .width(4)) multiplexer_6 (
    .in0(4'b0000), .in1(4'b1000), .in2(4'b1100), .out(ams), .sel({inst[30], inst[25]}));  // open: in3
  and and_1 (beq, not_1_out, not_2_out, not_3_out);
  and and_2 (bne, inst[12], not_4_out, not_5_out);
  and and_3 (blt, not_6_out, not_7_out, inst[14]);
  Multiplexer #(.enable("false"), .select(3), .width(4)) multiplexer_7 (
    .in0(ams), .in1(sllmulh), .in2(4'b0010), .in3(4'b1011), .in4(4'b0100), .in5(sr), .in6(4'b0110),
    .in7(4'b0111), .out(r_op), .sel(inst[14:12]));
  not not_8 (not_8_out, inst[2]);
  not not_9 (not_9_out, inst[3]);
  not not_10 (not_10_out, inst[4]);
  Multiplexer #(.enable("false"), .select(5)) multiplexer_8 (
    .in0(1'b1), .in4(1'b1), .in5(1'b1), .in8(1'b0), .in12(1'b1), .in13(1'b1), .in24(1'b0), .in25(1'b1),
    .in27(1'b1), .in28(1'b1), .out(RegWEn), .sel(inst[6:2]));  // open: in1, in2, in3, in6, in7, in9, in10, in11, in14, in15, in16, in17, in18, in19, in20, in21, in22, in23, in26, in29, in30, in31
  Multiplexer #(.enable("false"), .select(5), .width(2)) multiplexer_9 (
    .in0(2'b10), .in4(2'b01), .in5(2'b01), .in8(2'b11), .in12(2'b01), .in13(2'b01), .in24(2'b11),
    .in25(2'b00), .in27(2'b00), .in28(2'b11), .out(WBSel), .sel(inst[6:2]));  // open: in1, in2, in3, in6, in7, in9, in10, in11, in14, in15, in16, in17, in18, in19, in20, in21, in22, in23, in26, in29, in30, in31
  and and_4 (b_instr, not_8_out, not_9_out, not_10_out, inst[5], inst[6]);
  not not_11 (not_11_out, inst[13]);
  not not_12 (not_12_out, inst[12]);
  Multiplexer #(.enable("false"), .select(2), .width(4)) multiplexer_10 (
    .in0(4'b0001), .in1(4'b1001), .out(sllmulh), .sel({inst[30], inst[25]}));  // open: in2, in3
  and and_5 (bge, inst[12], not_11_out, inst[14]);
  and and_6 (bltu, not_12_out, inst[13], inst[14]);
  and and_7 (bgeu, inst[12], inst[13], inst[14]);
  Multiplexer #(.enable("false"), .select(3), .width(4)) multiplexer_11 (
    .in0(4'b0000), .in1(4'b0001), .in2(4'b0010), .in4(4'b0100), .in5(sr), .in6(4'b0110), .in7(4'b0111),
    .out(i_op), .sel(inst[14:12]));  // open: in3
  or or_1 (big, bge, bgeu);
  and and_8 (and_8_out, b_instr, or_2_out);
  Multiplexer #(.enable("false"), .select(3), .width(4)) multiplexer_12 (
    .in1(4'b0000), .in5(4'b1111), .out(csr_op), .sel(inst[14:12]));  // open: in0, in2, in3, in4, in6, in7
  Multiplexer #(.enable("false"), .select(2), .width(4)) multiplexer_13 (
    .in0(4'b0101), .in2(4'b1101), .out(sr), .sel({inst[30], inst[25]}));  // open: in1, in3
  and and_9 (and_9_out, smol, BrLt);
  Multiplexer #(.enable("false"), .select(5)) multiplexer_14 (
    .in0(1'b0), .in4(1'b0), .in5(1'b0), .in8(1'b0), .in12(1'b0), .in13(1'b0), .in24(br_uns), .in25(1'b0),
    .in27(1'b0), .in28(1'b0), .out(BrUn), .sel(inst[6:2]));  // open: in1, in2, in3, in6, in7, in9, in10, in11, in14, in15, in16, in17, in18, in19, in20, in21, in22, in23, in26, in29, in30, in31
  Multiplexer #(.enable("false"), .select(5)) multiplexer_15 (
    .in0(1'b0), .in4(1'b0), .in5(1'b0), .in8(1'b0), .in12(1'b0), .in13(1'b0), .in24(1'b0), .in25(1'b0),
    .in27(1'b0), .in28(1'b1), .out(CSRSel), .sel(inst[6:2]));  // open: in1, in2, in3, in6, in7, in9, in10, in11, in14, in15, in16, in17, in18, in19, in20, in21, in22, in23, in26, in29, in30, in31
  or or_2 (or_2_out, and_9_out, and_10_out, and_11_out, and_12_out);
  and and_10 (and_10_out, big, not_13_out);
  not not_13 (not_13_out, BrLt);
  or or_3 (smol, blt, bltu);
  Multiplexer #(.enable("false")) multiplexer_16 (.in0(1'b0), .in1(1'b1), .out(br_pc), .sel(and_8_out));
  and and_11 (and_11_out, beq, BrEq);
  and and_12 (and_12_out, bne, not_14_out);
  not not_14 (not_14_out, BrEq);
  and and_13 (br_uns, b_instr, or_4_out);
  Multiplexer #(.enable("false"), .select(5)) multiplexer_17 (
    .in0(1'b1), .in4(1'b1), .in5(1'b0), .in8(1'b1), .in12(1'b1), .in13(1'b0), .in24(1'b0), .in25(1'b1),
    .in27(1'b0), .in28(1'b0), .out(ASel), .sel(inst[6:2]));  // open: in1, in2, in3, in6, in7, in9, in10, in11, in14, in15, in16, in17, in18, in19, in20, in21, in22, in23, in26, in29, in30, in31
  Multiplexer #(.enable("false"), .select(5)) multiplexer_18 (
    .in0(1'b0), .in4(1'b0), .in5(1'b0), .in8(1'b0), .in12(1'b0), .in13(1'b0), .in24(1'b0), .in25(1'b0),
    .in27(1'b0), .in28(1'b1), .out(CSRWen), .sel(inst[6:2]));  // open: in1, in2, in3, in6, in7, in9, in10, in11, in14, in15, in16, in17, in18, in19, in20, in21, in22, in23, in26, in29, in30, in31
  or or_4 (or_4_out, bltu, bgeu);
  Multiplexer #(.enable("false"), .select(5)) multiplexer_19 (
    .in0(1'b1), .in4(1'b1), .in5(1'b1), .in8(1'b1), .in12(1'b0), .in13(1'b1), .in24(1'b1), .in25(1'b1),
    .in27(1'b1), .in28(1'b0), .out(BSel), .sel(inst[6:2]));  // open: in1, in2, in3, in6, in7, in9, in10, in11, in14, in15, in16, in17, in18, in19, in20, in21, in22, in23, in26, in29, in30, in31

  // Other names for the same wires on the sheet: funct7_bit1 = inst[25]; funct7_or_imm[6:0] = inst[31:25];
  //   smol_funct7[1:0] = {inst[30], inst[25]}; funct7_bit2 = inst[26]; funct7_bit3 = inst[27]; funct7_bit4 = inst[28];
  //   funct7_bit5 = inst[29]; funct7_bit6 = inst[30]; funct7_bit7 = inst[31]; opcode[6:0] = inst[6:0];
  //   op_bit3 = inst[2]; op_bit4 = inst[3]; op_bit5 = inst[4]; op_bit6 = inst[5]; op_bit7 = inst[6];
  //   rd_or_imm[4:0] = inst[11:7]; funct3[2:0] = inst[14:12]; funct3_bit1 = inst[12]; funct3_bit2 = inst[13];
  //   funct3_bit3 = inst[14]; rs1[4:0] = inst[19:15]; rs2[4:0] = inst[24:20]

  // Notes on the sheet:
  //   INPUTS to your circuit
  //   DON'T CHANGE THE LOCATIONS OF THE INPUTS AND OUTPUTS!
  //   OUTPUT from your circuit
endmodule
